# Fritzing sketch diagram (saved by Fritzing 0.9.3b)
breadboards: 1

parts:
  Part1 = Arduino Uno (Rev3)
  PART1 = ML8511 UV Sensor Breakout [part_number=SEN-12705]
  DHT1 = DHT11 Humitidy and Temperature Sensor
  Part2 = Standard LCD 16x2 white on blue [part_number=181]
  R3 = Rotary Potentiometer (Large) [maximum_resistance=100kΩ package=THT]
  U1 = POT [package=pot_alpha_rv16af-20]

nets:
  N1: Part1.A0, DHT1.DATA
  3V3: Part1.A4/SDA, Part1.3V3, PART1.EN, PART1.3.3V
  N2: Part1.A5/SCL, PART1.OUT
  N3: Part1.D8, Part2.DB7
  N4: Part1.D9_PWM, Part2.DB6
  N5: Part1.D10_PWM/SS, Part2.DB5
  N6: Part1.D11_PWM/MOSI, Part2.DB4
  N7: Part1.D12/MISO, Part2.E
  N8: Part1.D13/SCK, Part2.RS
  GND: Part1.GND, PART1.GND, DHT1.GND, Part2.VSS, Part2.R/W, Part2.LED-, R3.leg1
  VDD: Part1.5V, DHT1.VDD, Part2.VDD, R3.leg2, U1.A
  N9: Part2.V0, R3.wiper
  N10: Part2.LED+, U1.S

custom parts:
  ML8511 UV Sensor Breakout: Description: The ML8511 breakout is an easy to use ultraviolet light sensor. The MP8511 UV Sensor works by outputing an analog signal in relation to the amount of UV light it detects. This breakout can be very handy in creating devices that warn the user of sunburn or detect the UV index as it relates to weather conditions. This sensor breakout can detect 280-390nm light most effectively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
  DHT11 Humitidy and Temperature Sensor: DHT11 Humidity and Temperature Sensor
  Standard LCD 16x2 white on blue: Standard HD44780 LCDs are useful for creating standalone projects. * 16 characters wide, 2 rows * White text on blue background * Connection port is 0.1" pitch, single row for easy breadboarding and wiring
